// Logisim project FourBitAndGate.circ as structural Verilog: 1 circuit, main circuit main
module main (
  input  [3:0] in_1,
  input  [3:0] in_2,
  input  [3:0] in_3
);

  wire and_1_out, and_2_out, and_3_out, and_4_out, undriven, undriven_2, undriven_3, undriven_4, undriven_5,
       undriven_6, undriven_7, undriven_8;

  and and_1 (and_1_out, undriven, undriven_2);
  and and_2 (and_2_out, undriven_3, undriven_4);
  and and_3 (and_3_out, undriven_5, undriven_6);
  and and_4 (and_4_out, undriven_7, undriven_8);
endmodule
