// Logisim project Registerset4bit.circ as structural Verilog
module OneBitRegister (
  input  in_1,
  input  in_2,
  input  in_3,
  output out_4
);

  wire multiplexer_1_out;

  Multiplexer multiplexer_1 (.in0(out_4), .in1(in_1), .out(multiplexer_1_out), .sel(in_2));
  D_Flip_Flop d_ff_1 (.D(multiplexer_1_out), .clk(in_3), .Q(out_4));  // open: Qn, preset, reset
endmodule

module FourBitRegister (
  input  [3:0] in_1,
  input  in_2,
  input  in_3,
  output [3:0] out_4
);

  OneBitRegister onebitregister_1 (.in_1(in_1[3]), .in_2(in_2), .in_3(in_3), .out_4(out_4[3]));
  OneBitRegister onebitregister_2 (.in_1(in_1[2]), .in_2(in_2), .in_3(in_3), .out_4(out_4[2]));
  OneBitRegister onebitregister_3 (.in_1(in_1[1]), .in_2(in_2), .in_3(in_3), .out_4(out_4[1]));
  OneBitRegister onebitregister_4 (.in_1(in_1[0]), .in_2(in_2), .in_3(in_3), .out_4(out_4[0]));
endmodule

module RegisterSet (
  input  Enable,
  input  [2:0] Wr,
  input  [2:0] Ra,
  input  [3:0] Wrd,
  input  [2:0] Rb,
  output [3:0] A,
  output [3:0] B
);

  wire Clk_out, R1, R2, R3, R4, Ro;
  wire [3:0] r0, r1_t, r2_t, r3_t, r4_t;

  Decoder #(.select(3)) decoder_1 (
    .out0(Ro), .out1(R1), .out2(R2), .out3(R3), .out4(R4), .sel(Wr), .en(Enable));  // open: out5, out6, out7
  Clock Clk (.out(Clk_out));
  FourBitRegister fourbitregister_1 (.in_1(Wrd), .in_2(Ro), .in_3(Clk_out), .out_4(r0));
  FourBitRegister fourbitregister_2 (.in_1(Wrd), .in_2(R1), .in_3(Clk_out), .out_4(r1_t));
  FourBitRegister fourbitregister_3 (.in_1(Wrd), .in_2(R2), .in_3(Clk_out), .out_4(r2_t));
  FourBitRegister fourbitregister_4 (.in_1(Wrd), .in_2(R3), .in_3(Clk_out), .out_4(r3_t));
  FourBitRegister fourbitregister_5 (.in_1(Wrd), .in_2(R4), .in_3(Clk_out), .out_4(r4_t));
  Multiplexer #(.select(3), .width(4)) multiplexer_1 (
    .in0(r0), .in1(r1_t), .in2(r2_t), .in3(r3_t), .in4(r4_t), .out(A), .sel(Ra));  // open: in5, in6, in7
  Multiplexer #(.select(3), .width(4)) multiplexer_2 (
    .in0(r0), .in1(r1_t), .in2(r2_t), .in3(r3_t), .in4(r4_t), .out(B), .sel(Rb));  // open: in5, in6, in7

  // Notes on the sheet:
  //   A
  //   B
endmodule
